// Digital circuit SAP.dig as structural Verilog
module SAP (
  input  CLK,
  output [8:0] Control_in,
  output [3:0] Address_BUS,
  output [7:0] Data_BUS
);

  wire alu_1_c, alu_1_z, and_1_out, control_1_ai, control_1_ao, control_1_bi, control_1_ce, control_1_co,
       control_1_eo, control_1_fi, control_1_hlt, control_1_ii, control_1_io, control_1_mi, control_1_ri,
       control_1_ro, control_1_su, not_1_out;
  wire [3:0] ir_1_i_2;
  wire [7:0] alu_1_s, multiplexer_1_out, registera_1_a_2, registerb_1_p6, rom_1_d;

  Control control_1 (
    .IN(Control_in), .HLT(control_1_hlt), .MI(control_1_mi), .RI(control_1_ri), .RO(control_1_ro),
    .IO(control_1_io), .II(control_1_ii), .AI(control_1_ai), .EO(control_1_eo), .SU(control_1_su),
    .BI(control_1_bi), .CE(control_1_ce), .CO(control_1_co), .FI(control_1_fi), .AO(control_1_ao));  // open: OI, J
  not not_1 (not_1_out, control_1_hlt);
  and and_1 (and_1_out, CLK, not_1_out);
  RegisterA registera_1 (.A(Data_BUS), .CLK(and_1_out), .A_in(control_1_ai), .A_2(registera_1_a_2));
  Multiplexer #(.Bits(8)) multiplexer_1 (
    .sel(control_1_eo), .in_0(registerb_1_p6), .in_1({8{1'b0}}), .out(multiplexer_1_out));
  assign Data_BUS = control_1_ao ? registera_1_a_2 : 8'bz;  // Driver driver_1
  ALU alu_1 (.B(multiplexer_1_out), .A(registera_1_a_2), .Sub(control_1_su), .S(alu_1_s), .C(alu_1_c), .Z(alu_1_z));
  MAR mar_1 (.M(Data_BUS), .CLK(and_1_out), .M_in(control_1_mi), .M_2(Address_BUS));
  // FLAG flag_1: pin names not known; wires that end beside it: and_1_out, control_1_fi, alu_1_z, alu_1_c, Control_in[8], Control_in[7]
  // RegisterB registerb_1: pin names not known; wires that end beside it: and_1_out, control_1_ri, Data_BUS, and_1_out, control_1_bi, registerb_1_p6
  PC pc_1 (.en(control_1_ce), .CLK(and_1_out), .P_out(control_1_co), .P(Data_BUS));
  IR ir_1 (.I(Data_BUS), .CLK(and_1_out), .I_in(control_1_ii), .I_2({Control_in[6:3], ir_1_i_2}));  // open: Q
  assign Data_BUS = control_1_eo ? alu_1_s : 8'bz;  // Driver driver_2
  CC cc_1 (.en(1'b1), .CLK(and_1_out), .C0(Control_in[0]), .C1(Control_in[1]), .C2(Control_in[2]));
  ROM #(.AddrBits(4), .Bits(8)) rom_1 (.A(Address_BUS), .sel(1'b1), .D(rom_1_d));
  assign Data_BUS = control_1_io ? {Control_in[6:3], ir_1_i_2} : 8'bz;  // Driver driver_3
  assign Data_BUS = control_1_ro ? rom_1_d : 8'bz;  // Driver driver_4

  // Notes on the sheet:
  //   CLK: Hz: 2
  //   contents of rom_1 (hex, n*v repeats v):
  //   15,26,37,f0,0,1,4,3,4
endmodule
