// Digital circuit SAP_git.dig as structural Verilog
module SAP_git (
  input  CLK,
  input  clk_2,
  input  LT,
  input  clk_3,
  output [7:0] Data_BUS,
  output [7:0] A,
  output [7:0] B,
  output [7:0] PC,
  output C,
  output Z,
  output [3:0] OPCODE
);

  wire and_1_out, and_2_out, control_1_ai, control_1_ao, control_1_bi, control_1_ce, control_1_co,
       control_1_eo, control_1_fi, control_1_hlt, control_1_ii, control_1_io, control_1_j, control_1_mi,
       control_1_ri, control_1_ro, control_1_su, flag_1_p3, flag_1_p4, multiplexer_5_out, not_1_out;
  wire [2:0] cc_1_c2;
  wire [3:0] counter_1_out, ir_1_i_2, mar_1_m_2, multiplexer_2_out, multiplexer_3_out;
  wire [7:0] alu_1_s, blockramdualport_1_d, multiplexer_1_out, multiplexer_4_out, rom_1_d;

  not not_1 (not_1_out, control_1_hlt);
  CC cc_1 (.en(1'b1), .CLK(and_1_out), .C0(cc_1_c2[0]), .C1(cc_1_c2[1]), .C2(cc_1_c2[2]));
  and and_1 (and_1_out, CLK, not_1_out);
  Control control_1 (
    .IN({Z, C, OPCODE, cc_1_c2}), .HLT(control_1_hlt), .MI(control_1_mi), .RI(control_1_ri),
    .RO(control_1_ro), .IO(control_1_io), .II(control_1_ii), .AI(control_1_ai), .EO(control_1_eo),
    .SU(control_1_su), .BI(control_1_bi), .CE(control_1_ce), .CO(control_1_co), .J(control_1_j),
    .FI(control_1_fi), .AO(control_1_ao));  // open: OI
  // FLAG flag_1: pin names not known; wires that end beside it: and_1_out, control_1_fi, flag_1_p3, flag_1_p4, Z, C, and_1_out
  RegisterA registera_1 (.A(Data_BUS), .CLK(and_1_out), .A_in(control_1_ai), .A_2(A));
  // PC pc_1: pin names not known; wires that end beside it: control_1_ce, and_1_out, control_1_j, Data_BUS, PC
  and and_2 (and_2_out, control_1_io, control_1_ai);
  IR ir_1 (.I(Data_BUS), .CLK(and_1_out), .I_in(control_1_ii), .I_2({OPCODE, ir_1_i_2}));  // open: Q
  assign Data_BUS = control_1_co ? PC : 8'bz;  // Driver driver_1
  assign Data_BUS = control_1_ao ? A : 8'bz;  // Driver driver_2
  // RegisterB registerb_1: pin names not known; wires that end beside it: Data_BUS, and_1_out, control_1_bi, B
  MAR mar_1 (.M(Data_BUS), .CLK(and_1_out), .M_in(control_1_mi), .M_2(mar_1_m_2));
  Multiplexer #(.Bits(8)) multiplexer_1 (.sel(control_1_eo), .in_0(B), .in_1({8{1'b0}}), .out(multiplexer_1_out));
  ALU alu_1 (.B(multiplexer_1_out), .A(A), .SUB(control_1_su), .C(flag_1_p4), .Z(flag_1_p3), .S(alu_1_s));
  Multiplexer #(.Bits(4)) multiplexer_2 (.sel(and_2_out), .in_0(OPCODE), .in_1(4'b0000), .out(multiplexer_2_out));
  assign Data_BUS = control_1_io ? {multiplexer_2_out, ir_1_i_2} : 8'bz;  // Driver driver_3
  assign Data_BUS = control_1_eo ? alu_1_s : 8'bz;  // Driver driver_4
  ROM #(.AddrBits(4), .Bits(8)) rom_1 (.A(counter_1_out), .sel(1'b1), .D(rom_1_d));
  Multiplexer #(.Bits(4)) multiplexer_3 (.sel(LT), .in_0(mar_1_m_2), .in_1(counter_1_out), .out(multiplexer_3_out));
  Multiplexer #(.Bits(8)) multiplexer_4 (.sel(LT), .in_0(A), .in_1(rom_1_d), .out(multiplexer_4_out));
  Multiplexer multiplexer_5 (.sel(LT), .in_0(control_1_ri), .in_1(1'b1), .out(multiplexer_5_out));
  BlockRAMDualPort #(.AddrBits(4), .Bits(8)) blockramdualport_1 (
    .A(multiplexer_3_out), .Din(multiplexer_4_out), .str(multiplexer_5_out), .C(clk_2),
    .D(blockramdualport_1_d));
  assign Data_BUS = control_1_ro ? blockramdualport_1_d : 8'bz;  // Driver driver_5
  Counter #(.Bits(4)) counter_1 (.en(LT), .C(clk_3), .clr(1'b0), .out(counter_1_out));  // open: ovf

  // Notes on the sheet:
  //   CLK: Hz: 2
  //   clk_2: Hz: 100
  //   clk_3: Hz: 50
  //   contents of rom_1 (hex, n*v repeats v):
  //   1f,3e,88,76,51,f0,53,f0,52,f0,4*0,7f,80
endmodule
